// Digital circuit Acc8-seq.dig as structural Verilog
module Acc8_seq (
  input  EN,
  input  CLK,
  input  RST,
  output OVF,
  output [7:0] R
);

  wire [3:0] counter_1_out;
  wire [7:0] rom_1_d;

  Counter #(.Bits(4)) counter_1 (.en(EN), .C(CLK), .clr(RST), .out(counter_1_out));  // open: ovf
  ROM #(.AddrBits(4), .Bits(8)) rom_1 (.A(counter_1_out), .sel(EN), .D(rom_1_d));
  Acc8 acc8_1 (.A(rom_1_d), .CLK(EN), .RST(RST), .EN(CLK), .OVF(OVF), .R(R));

  // Notes on the sheet:
  //   contents of rom_1 (hex, n*v repeats v):
  //   1,2,1,2,1,2,1,2,1,2,1,2,1,2,1,2
endmodule
