// Digital circuit Acc8-seq_Q10.dig as structural Verilog
module Acc8_seq_Q10 (
  input  EN,
  input  CLK,
  input  RST,
  output OVF,
  output [7:0] R
);

  wire and_1_out, and_2_out, not_1_out, not_2_out, not_3_out, not_4_out, not_5_out;
  wire [3:0] counter_1_out;
  wire [7:0] rom_1_d;

  not not_1 (not_1_out, and_2_out);
  and and_1 (and_1_out, EN, not_1_out);
  Counter #(.Bits(4)) counter_1 (.en(and_1_out), .C(CLK), .clr(RST), .out(counter_1_out));  // open: ovf
  ROM #(.AddrBits(4), .Bits(8)) rom_1 (.A(counter_1_out), .sel(EN), .D(rom_1_d));
  and and_2 (and_2_out, rom_1_d[0], not_2_out, rom_1_d[2], not_3_out, rom_1_d[4], not_5_out, rom_1_d[6], not_4_out);
  not not_2 (not_2_out, rom_1_d[1]);
  not not_3 (not_3_out, rom_1_d[3]);
  not not_4 (not_4_out, rom_1_d[7]);
  not not_5 (not_5_out, rom_1_d[5]);
  Acc8 acc8_1 (.A(rom_1_d), .CLK(CLK), .RST(RST), .EN(and_1_out), .OVF(OVF), .R(R));

  // Notes on the sheet:
  //   contents of rom_1 (hex, n*v repeats v):
  //   1,2,1,2,1,2,55,2,1,2,1,2,1,2,1,2
endmodule
