// Digital circuit Acc8-seq_Q9.dig as structural Verilog
module Acc8_seq_Q9 (
  input  EN,
  input  CLK,
  input  RST,
  output OVF,
  output [7:0] R
);

  wire and_1_out, and_2_out, not_1_out;
  wire [3:0] counter_1_out;
  wire [7:0] rom_1_d;

  Counter #(.Bits(4)) counter_1 (.en(EN), .C(CLK), .clr(RST), .out(counter_1_out));  // open: ovf
  not not_1 (not_1_out, and_1_out);
  ROM #(.AddrBits(4), .Bits(8)) rom_1 (.A(counter_1_out), .sel(EN), .D(rom_1_d));
  and and_1 (and_1_out, rom_1_d[7], 1'b1);
  Acc8 acc8_1 (.A(rom_1_d), .CLK(CLK), .RST(RST), .EN(and_2_out), .OVF(OVF), .R(R));
  and and_2 (and_2_out, EN, not_1_out);

  // Notes on the sheet:
  //   contents of rom_1 (hex, n*v repeats v):
  //   1,1,1,80,2,2,2,2,1,2,1,2,1,2,1,2
endmodule
