// Digital circuit Acc8.dig as structural Verilog
module Acc8 (
  input  [7:0] A,
  input  CLK,
  input  RST,
  input  EN,
  output OVF,
  output [7:0] R
);

  wire xor_1_out;
  wire [7:0] addsub8_ovf_1_r;

  xor xor_1 (xor_1_out, EN, OVF);
  AddSub8_ovf addsub8_ovf_1 (.A(A), .B(R), .AS(1'b0), .R(addsub8_ovf_1_r), .OVF(OVF));
  // Reg8 reg8_1: pin names not known; wires that end beside it: CLK, addsub8_ovf_1_r, RST, xor_1_out, R
endmodule
