// Digital circuit Add8.dig as structural Verilog
module Add8 (
  input  A0,
  input  B0,
  input  Ci,
  input  B1,
  input  A1,
  input  B2,
  input  A2,
  input  B3,
  input  A3,
  input  B4,
  input  A4,
  input  B5,
  input  A5,
  input  B6,
  input  A6,
  input  B7,
  input  A7,
  output S0,
  output S1,
  output S2,
  output S3,
  output S4,
  output S5,
  output S6,
  output S7
);

  wire fa_1_co, fa_2_co, fa_3_co, fa_4_co, fa_5_co, fa_6_co, fa_7_co;

  FA fa_1 (.A(A0), .B(B0), .Ci(Ci), .Co(fa_1_co), .S(S0));
  FA fa_2 (.A(A1), .B(B1), .Ci(fa_1_co), .Co(fa_2_co), .S(S1));
  FA fa_3 (.A(A2), .B(B2), .Ci(fa_2_co), .Co(fa_3_co), .S(S2));
  FA fa_4 (.A(A3), .B(B3), .Ci(fa_3_co), .Co(fa_4_co), .S(S3));
  FA fa_5 (.A(A4), .B(B4), .Ci(fa_4_co), .Co(fa_5_co), .S(S4));
  FA fa_6 (.A(A5), .B(B5), .Ci(fa_5_co), .Co(fa_6_co), .S(S5));
  FA fa_7 (.A(A6), .B(B6), .Ci(fa_6_co), .Co(fa_7_co), .S(S6));
  FA fa_8 (.A(A7), .B(B7), .Ci(fa_7_co), .S(S7));  // open: Co
endmodule
