// Digital circuit AddSub8-ovf.dig as structural Verilog
module AddSub8_ovf (
  input  [7:0] A,
  input  [7:0] B,
  input  AS,
  output [7:0] R,
  output OVF
);

  AddSub8 addsub8_1 (.A(A), .AS(AS), .B(B), .R(R));
  det_OVF det_ovf_1 (.AS(AS), .sA(A[7]), .sB(B[7]), .sR(R[7]), .OVF(OVF));
endmodule
