// Digital circuit AddSub8.dig as structural Verilog
module AddSub8 (
  input  [7:0] A,
  input  AS,
  input  [7:0] B,
  output [7:0] R
);

  wire xor_1_out, xor_2_out, xor_3_out, xor_4_out, xor_5_out, xor_6_out, xor_7_out, xor_8_out;

  xor xor_1 (xor_1_out, B[0], AS);
  xor xor_2 (xor_2_out, B[1], AS);
  xor xor_3 (xor_3_out, B[2], AS);
  xor xor_4 (xor_4_out, B[3], AS);
  xor xor_5 (xor_5_out, B[4], AS);
  xor xor_6 (xor_6_out, B[5], AS);
  xor xor_7 (xor_7_out, B[6], AS);
  xor xor_8 (xor_8_out, B[7], AS);
  Add8 add8_1 (
    .A0(A[0]), .B0(xor_1_out), .Ci(AS), .B1(xor_2_out), .A1(A[1]), .B2(xor_3_out), .A2(A[2]), .B3(xor_4_out),
    .A3(A[3]), .B4(xor_5_out), .A4(A[4]), .B5(xor_6_out), .A5(A[5]), .B6(xor_7_out), .A6(A[6]),
    .B7(xor_8_out), .A7(A[7]), .S0(R[0]), .S1(R[1]), .S2(R[2]), .S3(R[3]), .S4(R[4]), .S5(R[5]), .S6(R[6]),
    .S7(R[7]));
endmodule
