// Digital circuit det-OVF.dig as structural Verilog
module det_OVF (
  input  AS,
  input  sA,
  input  sB,
  input  sR,
  output OVF
);

  wire and_1_out, and_2_out, and_3_out, and_4_out, not_1_out, not_2_out, not_3_out, not_4_out;

  not not_1 (not_1_out, AS);
  not not_2 (not_2_out, sA);
  not not_3 (not_3_out, sB);
  not not_4 (not_4_out, sR);
  and and_1 (and_1_out, not_1_out, not_2_out, not_3_out, sR);
  and and_2 (and_2_out, not_1_out, sA, sB, not_4_out);
  and and_3 (and_3_out, AS, not_2_out, sB, sR);
  and and_4 (and_4_out, AS, sA, not_3_out, not_4_out);
  or or_1 (OVF, and_1_out, and_2_out, and_3_out, and_4_out);
endmodule
